# Fritzing sketch wortuhr rpi zero (saved by Fritzing 0.9.3b)
breadboards: 1

parts:
  Raspberry_Pi_Zero1 = Raspberry Pi Zero
  RGB_SMD_LED1 = SMD RGB LED (WS2812) [package=5050]
  IC1 = MCP3008 8-channel 10-bit ADC [part_number=MCP3008]
  R1 = Resistor [tolerance=±5% resistance=220 package=THT]
  R2 = Photocell (LDR) [package=THT]
  R3 = Resistor [tolerance=±5% resistance=10k package="0805 [SMD]"]

nets:
  N1: Raspberry_Pi_Zero1.GPIO10, IC1.no_name_yet#3
  N2: Raspberry_Pi_Zero1.GPIO9, IC1.no_name_yet#4
  N3: Raspberry_Pi_Zero1.GPIO11, IC1.no_name_yet#5
  N4: Raspberry_Pi_Zero1.GND, RGB_SMD_LED1.NC, IC1.no_name_yet#1, IC1.no_name_yet#6, R3.Pin_1
  N5: Raspberry_Pi_Zero1.GPIO8, IC1.no_name_yet#2
  N6: Raspberry_Pi_Zero1.GPIO18, RGB_SMD_LED1.VDD
  5V: Raspberry_Pi_Zero1.5V, RGB_SMD_LED1.VSS, IC1.no_name_yet#7, IC1.no_name_yet#8, R1.Pin_1
  N7: IC1.no_name_yet#9, R2.pin_0, R3.Pin_0
  N8: R1.Pin_0, R2.pin_1

notes:
  LED Strip WS281x
